# Fritzing sketch boiler_agent (saved by Fritzing 0.9.3b)
circuit board: 8.46667cm x 5.64444cm
breadboards: 1

parts:
  U1 = atmega328 [package=dip]
  C1 = Capacitor [package=cap-pth-small2]
  R2 = Resistor [tolerance=±5% resistance=220 package=THT]
  D1 = LTE-302 [package=lte-302]
  C4_10uF = Capacitor Polarized [package=panasonic_d]
  XTAL1 = Crystal [frequency="8 MHz" package=THT]
  VCC1 = Battery
  C2 = Capacitor [package=cap-pth-small2]
  R1 = Resistor [tolerance=±5% resistance=10k package=THT]

nets:
  N1: U1.RESET, R1.Pin_1
  N2: U1.VCC, U1.AVCC, U1.AREF, C4_10uF.+, VCC1.+, R1.Pin_0
  GND: U1.GND, C1.1, D1.C, C4_10uF.-, VCC1.-, C2.1
  N3: U1.XLAT1, C1.2, XTAL1.pin_0
  N4: U1.XLAT2, XTAL1.pin_1, C2.2
  N5: U1.D13, R2.Pin_0
  N6: R2.Pin_1, D1.A
